# Fritzing sketch Schematic (saved by Fritzing 0.9.3b)
breadboards: 1

parts:
  Arduino_CNC_Shield_V3_00_1 = Arduino_CNC_V3.00
  M1 = Stepper Motor - Bipolar
  M2 = Stepper Motor - Bipolar
  Componente1 = Bluetooth HC-05 Macho
  KY-5 = Keyes Relay [package=THT]
  Power_Plug_12V = Power plug
  Arduino_Uno_Rev3 = Arduino Uno (Rev3) - ICSP
  KY-6 = Keyes Relay [package=THT]
  Power_Plug_7_5V = Power plug  # not connected
  L1 = Solenoid
  D1 = Rectifier Diode [part_number=1N4001 package="Melf DO-213 AB [SMD]"]  # not connected

nets:
  N1: Arduino_CNC_Shield_V3_00_1.Z.DIR, KY-5.signal
  N2: Arduino_CNC_Shield_V3_00_1.5V#11, KY-5.power, KY-5.C, KY-6.power
  N3: Arduino_CNC_Shield_V3_00_1.GND#12, KY-5.ground, KY-6.ground, L1.pin1
  N4: Arduino_CNC_Shield_V3_00_1.POWER_-, Power_Plug_12V.GND
  N5: Arduino_CNC_Shield_V3_00_1.POWER_+, KY-6.NO
  N6: Arduino_CNC_Shield_V3_00_1.X-MTR_'1', M1.A
  N7: Arduino_CNC_Shield_V3_00_1.X-MTR_'2', M1.C
  N8: Arduino_CNC_Shield_V3_00_1.X-MTR_'3', M1.B
  N9: Arduino_CNC_Shield_V3_00_1.X-MTR_'4', M1.D
  N10: Arduino_CNC_Shield_V3_00_1.Y-MTR_'1', M2.A
  N11: Arduino_CNC_Shield_V3_00_1.Y-MTR_'2', M2.C
  N12: Arduino_CNC_Shield_V3_00_1.Y-MTR_'3', M2.B
  N13: Arduino_CNC_Shield_V3_00_1.Y-MTR_'4', M2.D
  N14: Arduino_CNC_Shield_V3_00_1.SDA, Arduino_CNC_Shield_V3_00_1.GND#76, Componente1.GND
  3V3: Arduino_CNC_Shield_V3_00_1.5V#75, Arduino_CNC_Shield_V3_00_1.3V3, Componente1.VCC
  N15: Arduino_CNC_Shield_V3_00_1.End_Stops_Z+_(and_Z-)_/_SpnEn, Componente1.RXD
  N16: Arduino_CNC_Shield_V3_00_1.End_Stops_Z-_(and_Z+)_/_SpnEn, Arduino_CNC_Shield_V3_00_1.End_Stops_Y+_(and_Y-), Componente1.TXD, Arduino_Uno_Rev3.5V
  N17: Arduino_CNC_Shield_V3_00_1.End_Stops_Y-_(and_Y+), Arduino_Uno_Rev3.ICSP_MOSI
  N18: Arduino_CNC_Shield_V3_00_1.End_Stops_X+_(and_X-), Arduino_Uno_Rev3.GND, KY-6.signal
  N19: KY-5.NO, L1.pin2
  N20: Power_Plug_12V.VCC, KY-6.C

custom parts:
  Arduino_CNC_V3.00: Protoneer Arduino CNC Shield V3.00 If using Grbl V0.9: The “A” axis can not be used (yet). The “SCL” (Arduino A5) pin is now used for 'Probing' input. The “End Stops Z+ & Z-” (Arduino D11) and “SpnEn” (Arduino D12) have been switched!
  Keyes Relay: The Keyes 5V relay module is suitable for SCM development, home appliance control. It uses a 5V~12V TIL control signal which can control DC / AC signal.
